# Fritzing sketch fritzing (saved by Fritzing 0.9.3b)
breadboards: 1

parts:
  Parça1 = Arduino Uno (Rev3)
  hc-sr1 = hc-sr04
  J1 = Basic Servo

nets:
  N1: Parça1.D10_PWM/SS, hc-sr1.Trig
  N2: Parça1.D11_PWM/MOSI, hc-sr1.Echo
  N3: Parça1.D12/MISO, J1.pulse
  VCC: Parça1.5V, hc-sr1.VCC, J1.vcc
  GND: Parça1.GND, hc-sr1.GND, J1.gnd
